# Fritzing sketch Simple7SegmentDisplay_Sketch (saved by Fritzing 0.9.2b)
breadboards: 1

parts:
  Part1 = Arduino Uno (Rev3)
  7_Segment1 = 7 Segment Display
  R1 = Resistor [tolerance=±5% resistance=220 package="2512 [SMD]"]
  R2 = Resistor [tolerance=±5% resistance=220 package="2512 [SMD]"]
  R4 = Resistor [tolerance=±5% resistance=220 package="2512 [SMD]"]
  R5 = Resistor [tolerance=±5% resistance=220 package="2512 [SMD]"]
  R6 = Resistor [tolerance=±5% resistance=220 package="2512 [SMD]"]
  R7 = Resistor [tolerance=±5% resistance=220 package="2512 [SMD]"]
  R8 = Resistor [tolerance=±5% resistance=220 package="2512 [SMD]"]
  R9 = Resistor [tolerance=±5% resistance=220 package="2512 [SMD]"]
  7_Segment2 = 7 Segment Display  # not connected

nets:
  N1: Part1.D9_PWM, 7_Segment1.Segment_G, R2.Pin_1
  N2: Part1.D10_PWM/SS, 7_Segment1.Segment_F, R1.Pin_1
  N3: Part1.D11_PWM/MOSI, 7_Segment1.Segment_A, R4.Pin_1
  N4: Part1.D12/MISO, 7_Segment1.Segment_B, R5.Pin_1
  N5: Part1.D4, 7_Segment1.Segment_DP, R7.Pin_0
  N6: Part1.D5_PWM, 7_Segment1.Segment_C, R9.Pin_0
  N7: Part1.D6_PWM, 7_Segment1.Segment_D, R6.Pin_0
  N8: Part1.D7, 7_Segment1.Segment_E, R8.Pin_0
  N9: Part1.5V, R1.Pin_0, R2.Pin_0, R4.Pin_0, R5.Pin_0
  N10: Part1.GND, 7_Segment1.common_anode
  N11: R6.Pin_1, R7.Pin_1, R8.Pin_1, R9.Pin_1

notes:
  GND
  5V
  A
  B
  C
  D
  E
  F
  G
  DP
  PINs Layout
  A:7|B:6|C:4|D:2|E:1|F:9|G:10|DP:5
